// Logisim project ciruito_AND.circ as structural Verilog: 1 circuit, main circuit main
module main (
  input  A,
  input  B,
  output Saida_X
);

  wire AND_out;

  and AND (AND_out, A, B);
  not not_1 (Saida_X, AND_out);

  // Notes on the sheet:
  //   Entradas
  //   Negação
endmodule
